# Fritzing sketch WeMos_LEDstrip_Nextion_DHT (saved by Fritzing 0.9.3b)
circuit board: 7.32234cm x 8.19683cm
breadboards: 1

parts:
  R1 = Resistor [tolerance=±5% resistance=470 package=THT]
  IC1 = IC, DIP package, 20 pins [chip_label="SN74HCT245N " part_number=SN74HCT245N]
  C1 = Electrolytic Capacitor [capacitance=1µF package="100 mil [THT, electrolytic]"]
  F1 = FUSE [package=fuse_5mm]
  J2 = Screw terminal - 2 pins [package=THT]
  J3 = screw terminal, 3 pins
  WeMos_D1_Mini1 = WeMos D1 Mini
  DS1 = DS18B20 1-Wire Temperature Sensor [part_number=DS18B20]
  R4 = Resistor [tolerance=±5% resistance=4.7k package=THT]
  J4 = female pin header, 7 pins [form="♀ (female)"]
  J5 = female pin header, 7 pins [form="♀ (female)"]
  R5 = Resistor [tolerance=±5% resistance=10k package=THT]
  R6 = Resistor [tolerance=±5% resistance=10k package=THT]
  R7 = Resistor [tolerance=±5% resistance=10k package=THT]
  R8 = Resistor [tolerance=±5% resistance=10k package=THT]
  R9 = Resistor [tolerance=±5% resistance=10k package=THT]
  J6 = screw terminal, 3 pins
  R10 = Resistor [tolerance=±5% resistance=470 package=THT]
  J7 = screw terminal, 3 pins
  J8 = screw terminal, 3 pins
  R11 = Resistor [tolerance=±5% resistance=470 package=THT]
  R12 = Resistor [tolerance=±5% resistance=470 package=THT]
  J9 = female pin header, 2 pins [form="♀ (female)"]

nets:
  N1: R1.Pin_0, J3.pin2
  N2: R1.Pin_1, IC1.pin3
  N3: IC1.pin1, IC1.pin10, IC1.pin19, C1.-, J2.pin1, J3.pin1, WeMos_D1_Mini1.G, DS1.GND, J4.pin1, R5.Pin_1, R6.Pin_1, R7.Pin_1, R8.Pin_1, R9.Pin_1, J6.pin1, J7.pin1, J8.pin1, J9.pin1
  N4: IC1.pin4, R10.Pin_1
  N5: IC1.pin5, R11.Pin_1
  N6: IC1.pin6, R12.Pin_1
  N7: IC1.pin14, WeMos_D1_Mini1.D7
  N8: IC1.pin15, WeMos_D1_Mini1.D4
  N9: IC1.pin16, WeMos_D1_Mini1.TX
  N10: IC1.pin17, WeMos_D1_Mini1.RX
  N11: IC1.pin20, C1.+, F1.2, J3.pin3, WeMos_D1_Mini1.5V, J5.pin1, J6.pin3, J7.pin3, J8.pin3
  N12: F1.1, J2.pin2
  3V3: WeMos_D1_Mini1.3V3, DS1.VDD, R4.Pin_1, J5.pin2, J5.pin3, J5.pin4, J5.pin5, J5.pin6, J5.pin7
  N13: WeMos_D1_Mini1.A0, J4.pin7
  N14: WeMos_D1_Mini1.D0, J4.pin6, R9.Pin_0
  N15: WeMos_D1_Mini1.D1, J4.pin2, R5.Pin_0
  N16: WeMos_D1_Mini1.D2, J4.pin3, R6.Pin_0
  N17: WeMos_D1_Mini1.D3, DS1.DQ, R4.Pin_0
  N18: WeMos_D1_Mini1.D5, J4.pin5, R8.Pin_0
  N19: WeMos_D1_Mini1.D6, J4.pin4, R7.Pin_0
  N20: WeMos_D1_Mini1.RST, J9.pin2
  N21: J6.pin2, R10.Pin_0
  N22: J7.pin2, R11.Pin_0
  N23: J8.pin2, R12.Pin_0

notes:
  5V 3V3 D6 D5 D2 D1 GND
  GND D 5V
  GND 5V
  L  N  PE
  RST GND
  DH CW
  Deckenlampe
  Rev. 1.1
